# Fritzing sketch reefer (saved by Fritzing 0.9.2b)
breadboards: 1

parts:
  Raspberry_Pi1 = Raspberry Pi 2
  L293D = H-Bridge [package=THT]
  VCC1 = Battery
  M1 = DC Motor
  LED1 = LED - 5mm [color="Red (633nm)" package="5 mm [THT]"]
  LED2 = LED - 5mm [color="Red (633nm)" package="5 mm [THT]"]

nets (from the breadboard view):
  N1: Raspberry_Pi1.GPIO4, L293D.1A
  N2: Raspberry_Pi1.GPIO17, L293D.2A
  N3: Raspberry_Pi1.GPIO5, LED1.anode
  N4: Raspberry_Pi1.GPIO6, LED2.anode
  GND: Raspberry_Pi1.GND, L293D.GND4, VCC1.-, LED1.cathode, LED2.cathode
  N5: Raspberry_Pi1.GPIO18, L293D.1_2EN
  N6: Raspberry_Pi1.5V, L293D.VCC1
  N7: L293D.1Y, M1.pin_2
  N8: L293D.2Y, M1.pin_1
  N9: L293D.VCC2, VCC1.+
